# Fritzing sketch esquema-ligacao-portas-logicas-arduino-fritzenlab (saved by Fritzing 0.9.2b)

parts:
  Componente1 = Arduino Uno (Rev3)
  S1 = Pushbutton [package="[THT]"]
  S2 = Pushbutton [package="[THT]"]
  LED1 = smd LED [color="Red (633nm)" package="1206 [SMD]"]
  R1 = Resistor [tolerance=±5% resistance=2.2k package="0402 [SMD]"]
  R2 = Resistor [tolerance=±5% resistance=2.2k package="0402 [SMD]"]
  R3 = Resistor [tolerance=±5% resistance=2.2k package="0402 [SMD]"]

nets:
  N1: Componente1.GND, LED1.cathode, R1.Pin_1
  N2: Componente1.D2, S2.Pin_1, S2.Pin_2, R1.Pin_0
  N3: Componente1.D3_PWM, S1.Pin_2, R2.Pin_0
  N4: Componente1.5V, S1.Pin_3, S2.Pin_3, S2.Pin_4
  N5: LED1.anode, R3.Pin_0

notes:
  LED - Saida
  Entrada digital A
  Entrada digital B
